// Logisim project 8051.circ as structural Verilog: 5 circuits, main circuit main
module main (
  input  Reset,
  input  [7:0] in_2,
  input  IncrementtoPC,
  input  Resetto,
  output [7:0] out_5,
  output [15:0] out_6
);

  wire alu_v2_1_carryflag, alu_v2_1_zeroflag, CarryFlag, CLK_out, clock_1_out, clock_2_out,
       controlunit_1_incrementpc, controlunit_1_registerload, decoder_1_p1, decoder_1_p3, decoder_1_p5,
       decoder_1_p6, decoder_1_p7, decoder_1_p8, decoder_1_p9, decoder_1_p10, ZeroFlag;
  wire [3:0] controlunit_1_alu_opcode;
  wire [4:0] controlled_buffer_1_out, decoder_1_p4;
  wire [7:0] ALU_Buffer1_q, ALU_Buffer2_q, ALU_Output_q, alu_v2_1_accumulator, controlled_buffer_2_out,
       ControlUnitDataBuffer_q, RegisterA_q, RegisterB_q;
  wire [15:0] adder_1_out, adder_2_out, ProgramCounter_q;

  Clock clock_1 (.out(clock_1_out));
  Register #(.width(16)) ProgramCounter (
    .D(adder_1_out), .en(controlunit_1_incrementpc), .clk(clock_1_out), .Q(ProgramCounter_q), .clr(Reset));
  Clock clock_2 (.out(clock_2_out));
  Register #(.width(16)) register_1 (.D(adder_2_out), .en(IncrementtoPC), .clk(clock_2_out), .Q(out_6), .clr(Resetto));
  Adder #(.width(16)) adder_1 (
    .a(ProgramCounter_q), .out(adder_1_out), .cin(controlunit_1_incrementpc));  // open: b, cout
  ROM #(.addrWidth(16)) xCode (.addr(ProgramCounter_q), .data(out_5));
  Adder #(.width(16)) adder_2 (.a(out_6), .out(adder_2_out), .cin(IncrementtoPC));  // open: b, cout
  // NoConnect on decoder_1_p10
  // Decoder #(.select(5)) decoder_1: pin names not known; wires that end beside it: decoder_1_p1, decoder_1_p1, decoder_1_p3, decoder_1_p4, decoder_1_p5, decoder_1_p6, decoder_1_p7, decoder_1_p8, decoder_1_p9, decoder_1_p10
  ControlUnit controlunit_1 (
    .InstructionLine(in_2), .CarryFlag(CarryFlag), .ZeroFlag(ZeroFlag), .Reset(Reset),
    .RegisterAddress(decoder_1_p4), .ALU_Opcode(controlunit_1_alu_opcode),
    .RegisterLoad(controlunit_1_registerload), .RegisterStore(decoder_1_p3),
    .IncrementPC(controlunit_1_incrementpc));  // open: LockAluOpcode
  // NoConnect on decoder_1_p9
  Clock CLK (.out(CLK_out));
  Register ALU_Buffer1 (.D(controlled_buffer_2_out), .en(decoder_1_p5), .clk(CLK_out), .Q(ALU_Buffer1_q), .clr(Reset));
  Register ALU_Buffer2 (.D(controlled_buffer_2_out), .en(decoder_1_p6), .clk(CLK_out), .Q(ALU_Buffer2_q), .clr(Reset));
  Register RegisterA (.D(controlled_buffer_2_out), .en(decoder_1_p7), .clk(CLK_out), .Q(RegisterA_q), .clr(Reset));
  Register RegisterB (.D(controlled_buffer_2_out), .en(decoder_1_p8), .clk(CLK_out), .Q(RegisterB_q), .clr(Reset));
  Register ALU_Output (.D(alu_v2_1_accumulator), .en(1'b1), .clk(CLK_out), .Q(ALU_Output_q), .clr(Reset));
  assign controlled_buffer_1_out = controlunit_1_registerload ? decoder_1_p4 : 5'bz;  // Controlled_Buffer controlled_buffer_1
  ALU_v2 alu_v2_1 (
    .Buffer1(ALU_Buffer1_q), .Buffer2(ALU_Buffer2_q), .Opcode(controlunit_1_alu_opcode),
    .Accumulator(alu_v2_1_accumulator), .CarryFlag(alu_v2_1_carryflag), .ZeroFlag(alu_v2_1_zeroflag));  // open: OverflowIn, AuxiliaryCarryIn, CarryIn, ALU_OutputAux, SignFlag, AuxiliaryCarryFlag, OverflowFlag
  Register ControlUnitDataBuffer (
    .D(controlled_buffer_2_out), .en(controlunit_1_registerload), .clk(CLK_out), .Q(ControlUnitDataBuffer_q),
    .clr(Reset));
  assign controlled_buffer_2_out = decoder_1_p3 ? ControlUnitDataBuffer_q : 8'bz;  // Controlled_Buffer controlled_buffer_2
  PSW psw_1 (
    .CarryFlagIn(alu_v2_1_carryflag), .ZeroFlagIn(alu_v2_1_zeroflag), .CLK(CLK_out), .ZeroFlagOut(ZeroFlag),
    .CarryFlagOut(CarryFlag));
  Multiplexer #(.select(5), .width(8)) multiplexer_1 (
    .in2(RegisterA_q), .in3(RegisterB_q), .in4(ALU_Output_q), .out(controlled_buffer_2_out),
    .sel(controlled_buffer_1_out));  // open: in0, in1, in5, in6, in7, in8, in9, in10, in11, in12, in13, in14, in15, in16, in17, in18, in19, in20, in21, in22, in23, in24, in25, in26, in27, in28, in29, in30, in31

  // Notes on the sheet:
  //   contents of xCode (hex, n*v repeats v):
  //   30
  //   RegisterSelectBus
  //   registerAddressForInput
  //   Data Bus
  //   registerAddressForOutput
endmodule

module ALU_v2 (
  input  OverflowIn,
  input  AuxiliaryCarryIn,
  input  CarryIn,
  input  [7:0] Buffer1,
  input  [7:0] Buffer2,
  input  [3:0] Opcode,
  output [7:0] Accumulator,
  output [7:0] ALU_OutputAux,
  output CarryFlag,
  output ZeroFlag,
  output SignFlag,
  output AuxiliaryCarryFlag,
  output OverflowFlag
);

  wire adder_4_cout, adder_5_cout, adder_6_cout, adder_7_cout, adder_8_cout, adder_10_cout, comparator_1_lt,
       comparator_2_lt, comparator_3_lt, comparator_5_eq, comparator_5_gt, nor_1_out, or_1_out, xor_1_out,
       xor_2_out, xor_4_out;
  wire [6:0] adder_9_out, negator_2_out;
  wire [7:0] adder_1_out, adder_2_out, adder_3_out, adder_4_out, adder_5_out, adder_6_out, and_1_out,
       and_2_out, and_3_out, bit_extender_3_out, bit_extender_4_out, divider_1_out, divider_1_rem,
       multiplier_1_out, negator_1_out, or_2_out, shifter_1_out, shifter_2_out, undriven, xor_3_out;
  wire [15:0] bit_extender_1_out, bit_extender_2_out;
  wire [15:8] multiplier_1_out_2;

  Adder adder_1 (.a({8{1'b0}}), .b(Buffer2), .out(adder_1_out), .cin(CarryIn));  // open: cout
  Negator negator_1 (.in(adder_1_out), .out(negator_1_out));
  assign bit_extender_1_out = {{8{Buffer2[7]}}, Buffer2};  // Bit_Extender bit_extender_1
  assign bit_extender_2_out = {{8{Buffer1[7]}}, Buffer1};  // Bit_Extender bit_extender_2
  Comparator #(.mode("unsigned")) comparator_1 (.a(Buffer1), .b(Buffer2), .lt(comparator_1_lt));  // open: gt, eq
  Adder adder_2 (.a(8'h1), .b(Buffer1), .out(adder_2_out));  // open: cin, cout
  Adder adder_3 (.a({8{1'b1}}), .b(Buffer1), .out(adder_3_out));  // open: cin, cout
  Adder adder_4 (.a(Buffer1), .b(Buffer2), .out(adder_4_out), .cout(adder_4_cout));  // open: cin
  Adder adder_5 (.a(Buffer1), .b(Buffer2), .out(adder_5_out), .cin(CarryIn), .cout(adder_5_cout));
  Adder adder_6 (.a(Buffer1), .b(negator_1_out), .out(adder_6_out), .cout(adder_6_cout));  // open: cin
  Multiplier #(.width(16)) multiplier_1 (
    .a(bit_extender_1_out), .b(bit_extender_2_out), .out({multiplier_1_out_2, multiplier_1_out}));  // open: cin, cout
  Adder #(.width(4)) adder_7 (.a(Buffer1[3:0]), .b(Buffer2[3:0]), .cout(adder_7_cout));  // open: out, cin
  Adder #(.width(4)) adder_8 (.a(Buffer1[3:0]), .b(Buffer2[3:0]), .cin(CarryIn), .cout(adder_8_cout));  // open: out
  xor xor_1 (xor_1_out, CarryIn, adder_4_cout);
  Divider divider_1 (.a(Buffer1), .b(Buffer2), .out(divider_1_out), .rem(divider_1_rem));  // open: upper
  Comparator #(.mode("unsigned"), .width(4)) comparator_2 (
    .a(Buffer1[3:0]), .b(Buffer2[3:0]), .lt(comparator_2_lt));  // open: gt, eq
  xor xor_2 (xor_2_out, CarryIn, adder_5_cout);
  or or_1 (or_1_out, multiplier_1_out_2[8], multiplier_1_out_2[9], multiplier_1_out_2[10], multiplier_1_out_2[11], multiplier_1_out_2[12], multiplier_1_out_2[13], multiplier_1_out_2[14], multiplier_1_out_2[15]);
  nor nor_1 (nor_1_out, Buffer2[0], Buffer2[1], Buffer2[2], Buffer2[3], Buffer2[4], Buffer2[5], Buffer2[6], Buffer2[7]);
  Shifter #(.shift("rr")) shifter_1 (.in(Buffer1), .\dist (3'b001), .out(shifter_1_out));
  Shifter #(.shift("rl")) shifter_2 (.in(Buffer1), .\dist (3'b001), .out(shifter_2_out));
  // NoConnect on undriven
  assign or_2_out = Buffer1 | Buffer2;  // OR_Gate or_2, 8 bits wide
  assign and_1_out = Buffer1 & Buffer2;  // AND_Gate and_1, 8 bits wide
  assign xor_3_out = Buffer1 ^ Buffer2;  // XOR_Gate xor_3, 8 bits wide
  Comparator comparator_3 (.a(Buffer1), .b(Buffer2), .lt(comparator_3_lt));  // open: gt, eq
  Comparator #(.mode("unsigned")) comparator_4 (.a(Buffer1), .b(Buffer2), .eq(ZeroFlag), .lt(SignFlag));  // open: gt
  Adder #(.width(7)) adder_9 (.a({7{1'b0}}), .b(Buffer2[6:0]), .out(adder_9_out), .cin(CarryIn));  // open: cout
  Multiplexer #(.select(4), .width(8)) multiplexer_1 (
    .in0(adder_2_out), .in1(adder_3_out), .in2(adder_4_out), .in3(adder_5_out), .in4(adder_6_out),
    .in5(multiplier_1_out), .in6(divider_1_out), .in7(or_2_out), .in8(and_1_out), .in9(xor_3_out),
    .in10(undriven), .in11(shifter_1_out), .in12(shifter_1_out), .in13(shifter_2_out), .in14(shifter_2_out),
    .in15(Buffer1), .out(Accumulator), .sel(Opcode));
  Adder #(.width(7)) adder_10 (.a(Buffer1[6:0]), .b(negator_2_out), .cout(adder_10_cout));  // open: out, cin
  Negator #(.width(7)) negator_2 (.in(adder_9_out), .out(negator_2_out));
  Comparator #(.mode("unsigned"), .width(4)) comparator_5 (
    .a(Opcode), .b(4'b0101), .gt(comparator_5_gt), .eq(comparator_5_eq));  // open: lt
  xor xor_4 (xor_4_out, adder_6_cout, adder_10_cout);
  assign bit_extender_3_out = {{7{comparator_5_eq}}, comparator_5_eq};  // Bit_Extender bit_extender_3
  assign bit_extender_4_out = {{7{comparator_5_gt}}, comparator_5_gt};  // Bit_Extender bit_extender_4
  Multiplexer #(.select(4)) multiplexer_2 (
    .in0(CarryIn), .in1(CarryIn), .in2(adder_4_cout), .in3(adder_5_cout), .in4(comparator_1_lt), .in5(1'b0),
    .in6(1'b0), .in7(CarryIn), .in8(CarryIn), .in9(CarryIn), .in10(comparator_3_lt), .in12(Buffer1[0]),
    .in14(Buffer1[7]), .out(CarryFlag), .sel(Opcode));  // open: in11, in13, in15
  Multiplexer #(.select(4)) multiplexer_3 (
    .in0(CarryIn), .in1(CarryIn), .in2(adder_7_cout), .in3(adder_8_cout), .in4(comparator_2_lt),
    .in5(AuxiliaryCarryIn), .in6(AuxiliaryCarryIn), .in7(AuxiliaryCarryIn), .in8(AuxiliaryCarryIn),
    .in9(AuxiliaryCarryIn), .in10(AuxiliaryCarryIn), .out(AuxiliaryCarryFlag), .sel(Opcode));  // open: in11, in12, in13, in14, in15
  Multiplexer #(.select(4)) multiplexer_4 (
    .in0(CarryIn), .in1(CarryIn), .in2(xor_1_out), .in3(xor_2_out), .in4(xor_4_out), .in5(or_1_out),
    .in6(nor_1_out), .in7(OverflowIn), .in8(OverflowIn), .in9(OverflowIn), .in10(OverflowIn),
    .out(OverflowFlag), .sel(Opcode));  // open: in11, in12, in13, in14, in15
  assign and_2_out = bit_extender_3_out & multiplier_1_out_2;  // AND_Gate and_2, 8 bits wide
  assign and_3_out = bit_extender_4_out & divider_1_rem;  // AND_Gate and_3, 8 bits wide
  assign ALU_OutputAux = and_2_out | and_3_out;  // OR_Gate or_3, 8 bits wide

  // Notes on the sheet:
  //   ACC ->
  //   2. operand ->
  //   cin
  //   A
  //   B
endmodule

module ControlUnit (
  input  [7:0] InstructionLine,
  input  LockAluOpcode,
  input  CarryFlag,
  input  ZeroFlag,
  input  Reset,
  output [4:0] RegisterAddress,
  output [3:0] ALU_Opcode,
  output RegisterLoad,
  output RegisterStore,
  output IncrementPC
);

  wire clock_1_out, comparator_2_eq, jc_1_p2, multiplexer_1_out, or_1_out, undriven_3, undriven_4;
  wire [1:0] undriven_6;
  wire [3:0] ALU_OpcodeRegister_q, and_1_out, and_2_out, bit_extender_1_out, jc_1_p1, OpcodeToALU_Opcode_out,
       or_2_out, undriven, undriven_2, undriven_5;

  Clock clock_1 (.out(clock_1_out));
  // JC jc_1: pin names not known; wires that end beside it: jc_1_p1, jc_1_p2, undriven_6[1]
  PLA #(.in_width(8), .out_width(4), .\table ("00000011 1011 # rr\n00010011 1100 # rrc\n00100011 1101 # rl\n00110011 1110 # rlc\n0000x1xx 0000 # inc\n0001x1xx 0001 # dec\n0010x1xx 0010 # add\n0011x1xx 0011 # addc\n0100xx10 0111 # orl\n0101xx1x 1000 # anl\n1001x1xx 0100 # subb\n11011xxx 1010 # compare (djnz)")) OpcodeToALU_Opcode (
    .in(InstructionLine), .out(OpcodeToALU_Opcode_out));
  Comparator comparator_1 (.a(InstructionLine), .b(8'h40));  // open: gt, eq, lt
  Register #(.width(4)) ALU_OpcodeRegister (
    .D(OpcodeToALU_Opcode_out), .en(LockAluOpcode), .clk(clock_1_out), .Q(ALU_OpcodeRegister_q));  // open: clr
  // NoConnect on undriven_3
  // NoConnect on undriven_4
  Multiplexer #(.select(2)) multiplexer_1 (
    .in0(undriven_3), .in1(CarryFlag), .in2(ZeroFlag), .in3(undriven_4), .out(multiplexer_1_out),
    .sel(undriven_6));
  Comparator #(.mode("unsigned"), .width(4)) comparator_2 (
    .a(undriven_5), .b(4'b0000), .eq(comparator_2_eq));  // open: gt, lt
  assign bit_extender_1_out = {{3{multiplexer_1_out}}, multiplexer_1_out};  // Bit_Extender bit_extender_1
  or or_1 (or_1_out, undriven_6[0], undriven_6[1]);
  assign and_1_out = undriven_2 & bit_extender_1_out;  // AND_Gate and_1, 4 bits wide
  assign and_2_out = ~bit_extender_1_out & undriven;  // AND_Gate and_2, 4 bits wide
  Multiplexer #(.width(4)) multiplexer_2 (
    .in0(undriven_5), .in1(ALU_OpcodeRegister_q), .out(ALU_Opcode), .sel(comparator_2_eq));
  assign or_2_out = and_1_out | and_2_out;  // OR_Gate or_2, 4 bits wide
  SequenceGenerator sequencegenerator_1 (
    .LoadData(or_1_out), .Reset(jc_1_p2), .Data(or_2_out), .Value(jc_1_p1));  // open: Completed
endmodule

module SequenceGenerator (
  input  LoadData,
  input  Reset,
  input  [3:0] Data,
  output Completed,
  output [3:0] Value
);

  wire clock_1_out, not_1_out;

  Clock clock_1 (.out(clock_1_out));
  Counter #(.max('hf), .ongoal("stay"), .width(4)) counter_1 (
    .clr(Reset), .load(LoadData), .up(1'b1), .count(not_1_out), .clk(clock_1_out), .D(Data),
    .carry(Completed), .Q(Value));
  not not_1 (not_1_out, Reset);
endmodule

module PSW (
  input  CarryFlagIn,
  input  ZeroFlagIn,
  input  CLK,
  output ZeroFlagOut,
  output CarryFlagOut
);

  D_Flip_Flop ZeroFlag (.D(ZeroFlagIn), .clk(CLK), .Q(ZeroFlagOut));  // open: Qn, preset, reset
  D_Flip_Flop CarryFlag (.D(CarryFlagIn), .clk(CLK), .Q(CarryFlagOut));  // open: Qn, preset, reset
endmodule
